// Logisim project SAP-1.circ as structural Verilog
module program_counter (
  input  Ep,
  input  Cp,
  input  nCLR,
  input  nCLK
);

  wire n74ls107_1_q1, n74ls107_1_q2, n74ls107_2_q1, n74ls107_2_q2, n74ls126_1__1y, n74ls126_1__2y,
       n74ls126_1__3y, n74ls126_1__4y;

  _74LS107 u_74ls107_1 (
    .J1(Cp), .CLK1(nCLK), .K1(Cp), .nCLR1(nCLR), .J2(Cp), .CLK2(n74ls107_1_q1), .K2(Cp), .nCLR2(nCLR),
    .Vcc(1'b1), .Gnd(1'b0), .Q1(n74ls107_1_q1), .Q2(n74ls107_1_q2));  // open: Q_n1, Q_n1_2
  _74LS107 u_74ls107_2 (
    .J1(Cp), .CLK1(n74ls107_1_q2), .K1(Cp), .nCLR1(nCLR), .J2(Cp), .CLK2(n74ls107_2_q1), .K2(Cp),
    .nCLR2(nCLR), .Vcc(1'b1), .Gnd(1'b0), .Q1(n74ls107_2_q1), .Q2(n74ls107_2_q2));  // open: Q_n1, Q_n1_2
  _74LS126 u_74ls126_1 (
    .GND(1'b0), .Vcc(1'b1), ._1A(n74ls107_1_q1), ._1G(Ep), ._2A(n74ls107_1_q2), ._2G(Ep),
    ._3A(n74ls107_2_q1), ._3G(Ep), ._4A(n74ls107_2_q2), ._4G(Ep), ._1Y(n74ls126_1__1y), ._2Y(n74ls126_1__2y),
    ._3Y(n74ls126_1__3y), ._4Y(n74ls126_1__4y));

  // Notes on the sheet:
  //   B0
  //   B1
  //   B2
  //   B3
endmodule

module _74LS107 (
  input  J1,
  input  CLK1,
  input  K1,
  input  nCLR1,
  input  J2,
  input  CLK2,
  input  K2,
  input  nCLR2,
  input  Vcc,
  input  Gnd,
  output Q1,
  output Q_n1,
  output Q2,
  output Q_n1_2
);

  wire not_1_out, not_2_out, not_3_out, not_4_out;

  not not_1 (not_1_out, CLK1);
  not not_2 (not_2_out, nCLR1);
  not not_3 (not_3_out, CLK2);
  not not_4 (not_4_out, nCLR2);
  J_K_Flip_Flop j_k_ff_1 (.J(J1), .clk(not_1_out), .K(K1), .Q(Q1), .Qn(Q_n1), .reset(not_2_out));  // open: preset, en
  J_K_Flip_Flop j_k_ff_2 (.J(J2), .clk(not_3_out), .K(K2), .Q(Q2), .Qn(Q_n1_2), .reset(not_4_out));  // open: preset, en
endmodule

module _74LS126 (
  input  GND,
  input  Vcc,
  input  _1A,
  input  _1G,
  input  _2A,
  input  _2G,
  input  _3A,
  input  _3G,
  input  _4A,
  input  _4G,
  output _1Y,
  output _2Y,
  output _3Y,
  output _4Y
);

  assign _1Y = _1G ? _1A : 1'bz;  // Controlled_Buffer controlled_buffer_1
  assign _2Y = _2G ? _2A : 1'bz;  // Controlled_Buffer controlled_buffer_2
  assign _3Y = _3G ? _3A : 1'bz;  // Controlled_Buffer controlled_buffer_3
  assign _4Y = _4G ? _4A : 1'bz;  // Controlled_Buffer controlled_buffer_4
endmodule
